# Fritzing sketch tmp102_7seg (saved by Fritzing 0.9.1b)
breadboards: 1

parts:
  Part1 = Arduino Uno (Rev3) - ICSP
  Part2 = Digital Temperature Sensor Breakout - TMP102
  U1 = 74HC595 SMD [package="SO16 [SMD]"]
  LED1 = 7-SEGMENT-4DIGIT-YOUNGSUN [package=7-segment-4digit-youngsun-longpads]
  R1 = Resistor [tolerance=±5% resistance=220 package="0603 [SMD]"]
  R2 = Resistor [tolerance=±5% resistance=220 package="0603 [SMD]"]
  R3 = Resistor [tolerance=±5% resistance=220 package="0603 [SMD]"]
  R4 = Resistor [tolerance=±5% resistance=220 package="0603 [SMD]"]

nets:
  N1: Part1.A4/SDA, Part2.SDA
  N2: Part1.D8, U1.MR
  N3: Part1.D11_PWM/MOSI, U1.DS
  N4: Part1.D12/MISO, U1.SH_CP
  N5: Part1.D1/TX, R4.Pin_0
  N6: Part1.D2, R3.Pin_0
  N7: Part1.D3_PWM, R2.Pin_0
  N8: Part1.D4, R1.Pin_0
  GND: Part2.GND, U1.GND
  N9: U1.Q1, LED1.B
  N10: U1.Q2, LED1.C
  N11: U1.Q3, LED1.D
  N12: U1.Q4, LED1.COL-A
  N13: U1.Q5, LED1.APOS-A
  N14: U1.Q6, LED1.G
  N15: U1.Q7, LED1.DP
  N16: U1.Q0, LED1.A
  N17: LED1.DIG1, R4.Pin_1
  N18: LED1.DIG2, R3.Pin_1
  N19: LED1.DIG3, R2.Pin_1
  N20: LED1.DIG4, R1.Pin_1
